// Logisim project Somador carry lookahead 2.circ as structural Verilog: 1 circuit, main circuit main
module main (
  input  A4,
  input  B4,
  input  A3,
  input  B3,
  input  A2,
  input  B2,
  input  A1,
  input  B1,
  input  Cin,
  output S,
  output S_2,
  output S_3,
  output S_4,
  output S_5
);

  wire and_1_out, and_2_out, and_3_out, and_4_out, and_5_out, and_6_out, and_7_out, and_8_out, and_9_out,
       and_10_out, Co1_out, Co2_out, Co3_out, G1_out, G2_out, G3_out, G4_out, P1_out, P2_out, P3_out, P4_out;

  or Co4 (S, G4_out, and_1_out, and_2_out, and_3_out, and_4_out);
  and G4 (G4_out, A4, B4);
  and and_1 (and_1_out, P4_out, G3_out);
  and and_2 (and_2_out, P4_out, P3_out, G2_out);
  and and_3 (and_3_out, P4_out, P3_out, P2_out, G1_out);
  and and_4 (and_4_out, P4_out, P3_out, P2_out, P1_out, Cin);
  or P4 (P4_out, A4, B4);
  or Co3 (Co3_out, G3_out, and_5_out, and_6_out, and_7_out);
  Adder #(.width(1)) adder_1 (.a(A4), .b(B4), .out(S_2), .cin(Co3_out));  // open: cout
  and and_5 (and_5_out, P3_out, G2_out);
  and and_6 (and_6_out, P3_out, P2_out, G1_out);
  and G3 (G3_out, A3, B3);
  and and_7 (and_7_out, P3_out, P2_out, P1_out, Cin);
  or P3 (P3_out, A3, B3);
  or Co2 (Co2_out, G2_out, and_8_out, and_9_out);
  and and_8 (and_8_out, P2_out, G1_out);
  and and_9 (and_9_out, P2_out, P1_out, Cin);
  Adder #(.width(1)) adder_2 (.a(A3), .b(B3), .out(S_3), .cin(Co2_out));  // open: cout
  and G2 (G2_out, A2, B2);
  or P2 (P2_out, A2, B2);
  or Co1 (Co1_out, G1_out, and_10_out);
  and and_10 (and_10_out, P1_out, Cin);
  Adder #(.width(1)) adder_3 (.a(A2), .b(B2), .out(S_4), .cin(Co1_out));  // open: cout
  and G1 (G1_out, A1, B1);
  or P1 (P1_out, A1, B1);
  Adder #(.width(1)) adder_4 (.a(A1), .b(B1), .out(S_5), .cin(Cin));  // open: cout
endmodule
